# Fritzing sketch pi-boot-arduino (saved by Fritzing 0.9.1b)
breadboards: 2

parts:
  Part1 = Arduino Uno (Rev3)
  J1 = T Cobbler Plus  # not connected
  Part2 = Logic Level Converter
  Part3 = Logic Level Converter

nets:
  N1: Part1.D11_PWM/MOSI, Part2.TX_HV
  N2: Part1.D12/MISO, Part2.TX2_HV
  N3: Part1.D13/SCK, Part3.TX_HV
  N4: Part1.RESET, Part1.GND
  N5: Part1.5V, Part2.HV
  GND: Part2.GND, Part3.GND
  N6: Part2.LV, Part3.LV

custom parts:
  T Cobbler Plus: The T-Cobbler Plus is an add on prototyping board from Adafruit specifically designed for the Raspberry Pi B+ that can break out all those tasty power, GPIO, I2C and SPI pins from the 40-pin header onto a solderless breadboard. This set will make "cobbling together" prototypes with the Pi super easy. The T-Cobbler Plus can plug into any solderless breadboard.
