# Fritzing sketch pi-boot (saved by Fritzing 0.9.1b)
breadboards: 3

parts:
  Part2 = Logic Level Converter
  Part3 = Logic Level Converter
  U1 = atmega328 [package=dip]
  XTAL1 = Crystal [frequency="16 Mhz" package=THT]
  C1 = Ceramic Capacitor [capacitance=100nF package="100 mil [THT, multilayer]"]
  C2 = Ceramic Capacitor [capacitance=100nF package="100 mil [THT, multilayer]"]
  J2 = T Cobbler Plus

nets (from the schematic view):
  N1: Part2.TX2_LV, J2.MOSI
  N2: Part2.GND, J2.GND#5
  N3: Part2.LV, Part3.LV, J2.3V3
  N4: Part2.TX_LV, J2.SCLK
  N5: Part2.TX_HV, U1.D13
  N6: Part2.HV, Part3.HV, U1.AVCC, J2.5.0V#3
  N7: Part2.TX2_HV, U1.D12
  N8: Part3.GND, U1.GND#21
  N9: Part3.TX_LV, J2.MISO
  N10: Part3.TX_HV, U1.D11_(PWM)
  N11: U1.RESET, U1.GND#7, C1.0, C2.0
  N12: U1.XLAT1, XTAL1.pin_0, C1.1
  N13: U1.XLAT2, XTAL1.pin_1, C2.1

custom parts:
  T Cobbler Plus: The T-Cobbler Plus is an add on prototyping board from Adafruit specifically designed for the Raspberry Pi B+ that can break out all those tasty power, GPIO, I2C and SPI pins from the 40-pin header onto a solderless breadboard. This set will make "cobbling together" prototypes with the Pi super easy. The T-Cobbler Plus can plug into any solderless breadboard.
